# Fritzing sketch Texugo (saved by Fritzing 0.9.3b)
perfboards: 1

parts:
  Raspberry_Pi_Zero2 = Raspberry Pi Zero  # not connected
  J1 = female pin header, 3 pins [form="♀ (female)"]
  J2 = female pin header, 3 pins [form="♀ (female)"]
  J3 = female pin header, 3 pins [form="♀ (female)"]
  J4 = female pin header, 3 pins [form="♀ (female)"]
  J5 = female pin header, 2 pins [form="♀ (female)"]
  J6 = male pin header, 20 pins [form="♂ (male)"]
  J7 = male pin header, 2 pins [form="♂ (male)"]
  J8 = female pin header, 3 pins [form="♀ (female)"]  # not connected
  J9 = male pin header, 3 pins [form="♂ (male)"]  # not connected

nets:
  N1: J1.pin1, J6.pin4
  N2: J1.pin2, J6.pin8
  N3: J1.pin3, J2.pin2
  N4: J2.pin1, J6.pin2
  N5: J2.pin3, J4.pin2, J5.pin1, J6.pin16
  N6: J3.pin1, J6.pin19
  N7: J3.pin2, J6.pin18
  N8: J4.pin1, J5.pin2, J7.pin2
  N9: J4.pin3, J6.pin17

notes:
  Texugo board v0.2
